// Logisim project 11.gates_RT_TT.circ as structural Verilog: 1 circuit, main circuit main
module main (
);

  wire clock_1_out, clock_2_out, pull_resistor_1_node, transistor_2_out;

  Clock clock_1 (.out(clock_1_out));
  Pull_Resistor #(.pull(1)) pull_resistor_1 (.node(pull_resistor_1_node));
  Transistor #(.\type ("n")) transistor_1 (.in(1'b0), .out(pull_resistor_1_node), .gate(clock_2_out));
  Clock #(.highDuration(10), .lowDuration(10)) clock_2 (.out(clock_2_out));
  Transistor transistor_2 (.in(1'b1), .out(transistor_2_out), .gate(clock_2_out));
  Transistor #(.\type ("n")) transistor_3 (.in(1'b0), .out(transistor_2_out), .gate(clock_2_out));
  // Digital_Oscilloscope digital_oscilloscope_1: pin names not known; wires that end beside it: clock_1_out, clock_2_out, pull_resistor_1_node, transistor_2_out
endmodule
