// Logisim project 12.Arithm_Plex_Mem.1.Adder.circ as structural Verilog: 3 circuits, main circuit Half_Adder
// +/2
module Half_Adder (
  input  a,
  input  b,
  output s,
  output c
);

  xor xor_1 (s, a, b);
  and and_1 (c, a, b);

  // Notes on the sheet:
  //   1. Полусумматор
endmodule

// +
module Full_Adder (
  input  c_in,
  input  a,
  input  b,
  output s,
  output c_out
);

  wire half_adder_1_c, half_adder_1_s, half_adder_2_c;

  Half_Adder half_adder_1 (.a(a), .b(b), .s(half_adder_1_s), .c(half_adder_1_c));
  Half_Adder half_adder_2 (.a(c_in), .b(half_adder_1_s), .s(s), .c(half_adder_2_c));
  or or_1 (c_out, half_adder_2_c, half_adder_1_c);

  // Notes on the sheet:
  //   2. Полный одноразрядный сумматор
endmodule

module Multibit_Adder (
  input  c_in,
  input  a_0,
  input  a_1,
  input  a_2,
  input  a_3,
  input  b_0,
  input  b_1,
  input  b_2,
  input  b_3,
  output s_0,
  output s_1,
  output s_2,
  output s_3,
  output c_out
);

  wire full_adder_1_c_out, full_adder_2_c_out, full_adder_3_c_out;

  Full_Adder full_adder_1 (.c_in(c_in), .a(a_0), .b(b_0), .s(s_0), .c_out(full_adder_1_c_out));
  Full_Adder full_adder_2 (.c_in(full_adder_1_c_out), .a(a_1), .b(b_1), .s(s_1), .c_out(full_adder_2_c_out));
  Full_Adder full_adder_3 (.c_in(full_adder_2_c_out), .a(a_2), .b(b_2), .s(s_2), .c_out(full_adder_3_c_out));
  Full_Adder full_adder_4 (.c_in(full_adder_3_c_out), .a(a_3), .b(b_3), .s(s_3), .c_out(c_out));

  // Notes on the sheet:
  //   3. Многоразрядный сумматор
endmodule
