// Logisim project 12.Arithm_Plex_Mem.2.Coders_Plexors.circ as structural Verilog: 2 circuits, main circuit Encoder
module Encoder (
  input  i_0,
  input  i_1,
  input  i_2,
  input  i_3,
  output o_0,
  output o_1
);

  or or_1 (o_0, i_1, i_3);
  or or_2 (o_1, i_2, i_3);

  // Notes on the sheet:
  //   1. Шифратор
endmodule

module Dec0der (
  input  i_1,
  input  i_0,
  output o_0,
  output o_1,
  output o_2,
  output o_3
);

  wire not_1_out, not_2_out;

  and and_1 (o_0, not_1_out, not_2_out);
  not not_1 (not_1_out, i_1);
  not not_2 (not_2_out, i_0);
  and and_2 (o_1, not_1_out, i_0);
  and and_3 (o_2, i_1, not_2_out);
  and and_4 (o_3, i_1, i_0);

  // Notes on the sheet:
  //   1. Дешифратор
endmodule
