// Logisim project 12.Arithm_Plex_Mem.3.PLD.circ as structural Verilog: 1 circuit, main circuit main
module main (
  input  A,
  input  B,
  input  C,
  output F0,
  output F1,
  output F2
);

  wire and_1_out, and_2_out, and_3_out, and_4_out, not_1_out, not_2_out, not_3_out;

  not not_1 (not_1_out, A);
  not not_2 (not_2_out, B);
  not not_3 (not_3_out, C);
  and and_1 (and_1_out, not_3_out, B);
  and and_2 (and_2_out, C, A);
  and and_3 (and_3_out, not_2_out, not_1_out);
  and and_4 (and_4_out, B, not_1_out);
  or or_1 (F0, and_1_out, and_2_out);
  or or_2 (F1, and_1_out, and_3_out);
  or or_3 (F2, and_4_out, and_2_out);

  // Notes on the sheet:
  //   Поле OR ----->
  //   <----- Поле AND
endmodule
