// Logisim project 13.Triggers_Registers.3.JKC_T.circ as structural Verilog: 1 circuit, main circuit main
module main (
  input  J,
  input  K,
  input  T,
  input  T_2,
  output Q,
  output nQ,
  output out_7,
  output out_8
);

  wire and_1_out, and_2_out, d_ff_1_qn, or_1_out;

  or or_1 (or_1_out, J, K);
  D_Flip_Flop d_ff_1 (.clk(T_2), .D(d_ff_1_qn), .Q(out_8), .Qn(d_ff_1_qn));  // open: preset, reset
  and and_1 (and_1_out, nQ, J);
  and and_2 (and_2_out, K, Q);
  J_K_Flip_Flop j_k_ff_1 (.J(T), .clk(T), .K(T), .Q(out_7));  // open: Qn, preset, reset
  S_R_Flip_Flop s_r_ff_1 (.S(and_1_out), .clk(or_1_out), .R(and_2_out), .Q(Q), .Qn(nQ));  // open: preset, reset

  // Notes on the sheet:
  //   1. JK-триггер
  //   2.a. T-триггер на базе JK
  //   2.b. T-триггер на базе D
endmodule
