// Logisim project 13.Triggers_Registers.5.Shifter.circ as structural Verilog: 1 circuit, main circuit main
module main (
  input  W,
  input  D,
  input  W_2,
  input  in_4,
  input  [3:0] D_2,
  input  S,
  output [3:0] out_7,
  output [3:0] out_8,
  output [3:0] out_9
);

  wire [3:0] multiplexer_1_out;

  D_Flip_Flop d_ff_1 (.clk(W), .D(D), .Q(out_7[0]));  // open: Qn, preset, reset
  D_Flip_Flop d_ff_2 (.clk(W_2), .D(multiplexer_1_out[0]), .Q(out_8[0]));  // open: Qn, preset, reset
  D_Flip_Flop d_ff_3 (.clk(W), .D(out_7[0]), .Q(out_7[1]));  // open: Qn, preset, reset
  D_Flip_Flop d_ff_4 (.clk(W_2), .D(multiplexer_1_out[1]), .Q(out_8[1]));  // open: Qn, preset, reset
  D_Flip_Flop d_ff_5 (.clk(W), .D(out_7[1]), .Q(out_7[2]));  // open: Qn, preset, reset
  D_Flip_Flop d_ff_6 (.clk(W_2), .D(multiplexer_1_out[2]), .Q(out_8[2]));  // open: Qn, preset, reset
  D_Flip_Flop d_ff_7 (.clk(W), .D(out_7[2]), .Q(out_7[3]));  // open: Qn, preset, reset
  D_Flip_Flop d_ff_8 (.clk(W_2), .D(multiplexer_1_out[3]), .Q(out_8[3]));  // open: Qn, preset, reset
  Multiplexer #(.enable("false"), .width(4)) multiplexer_1 (
    .in0(D_2), .in1({out_8[2:0], in_4}), .out(multiplexer_1_out), .sel(S));

  assign out_9 = {out_8[2:0], in_4};

  // Notes on the sheet:
  //   1. Сдвигающий регистр (загружающий)
  //   2. Сдвигающий регистр (выгружающий)... Всё, нужны мультиплексоры!
endmodule
