// Logisim project 13.Triggers_Registers.6.Just_A_Register.circ as structural Verilog: 1 circuit, main circuit main
module main (
  input  [3:0] in_1,
  input  W,
  input  in_3,
  input  in_4,
  input  [3:0] \Ноги ,
  output [3:0] out_6
);

  wire [3:0] multiplexer_2_out, register_1_q;

  Multiplexer #(.enable("false"), .width(4)) multiplexer_1 (.in0(register_1_q), .in1(\Ноги ), .out(out_6), .sel(in_4));
  Multiplexer #(.enable("false"), .width(4)) multiplexer_2 (
    .in0(in_1), .in1(out_6), .out(multiplexer_2_out), .sel(in_3));
  Register #(.width(4)) register_1 (.D(multiplexer_2_out), .Q(register_1_q), .clk(W));  // open: en, clr

  // Notes on the sheet:
  //   1. Просто регистр =)
  //   Откуда загрузка в регистр
  //   Откуда данные на шине
  //   Шина данных внутри процесора
endmodule
