// Logisim project 21.R16.circ as structural Verilog: 3 circuits, main circuit R16CPU
module R16File (
  input  [15:0] WDz,
  input  [3:0] RAx,
  input  [3:0] RAy,
  input  [3:0] WAz,
  input  Wz,
  output [15:0] RDx,
  output [15:0] RDy
);

  wire decoder_1_out1, decoder_1_out2, decoder_1_out3, decoder_1_out4, decoder_1_out5, decoder_1_out6,
       decoder_1_out7, decoder_1_out8, decoder_1_out9, decoder_1_out10, decoder_1_out11, decoder_1_out12,
       decoder_1_out13, decoder_1_out14, decoder_1_out15;
  wire [15:0] R1_q, R2_q, R3_q, R4_q, R5_q, R6_q, R7_q, R8_q, R9_q, R10_q, R11_q, R12_q, R13_q, R14_q, R15_q;

  Decoder #(.select(4)) decoder_1 (
    .out1(decoder_1_out1), .out2(decoder_1_out2), .out3(decoder_1_out3), .out4(decoder_1_out4),
    .out5(decoder_1_out5), .out6(decoder_1_out6), .out7(decoder_1_out7), .out8(decoder_1_out8),
    .out9(decoder_1_out9), .out10(decoder_1_out10), .out11(decoder_1_out11), .out12(decoder_1_out12),
    .out13(decoder_1_out13), .out14(decoder_1_out14), .out15(decoder_1_out15), .sel(WAz), .en(1'b1));  // open: out0
  Register #(.width(16)) R1 (.D(WDz), .en(decoder_1_out1), .clk(Wz), .Q(R1_q));  // open: clr
  Register #(.width(16)) R2 (.D(WDz), .en(decoder_1_out2), .clk(Wz), .Q(R2_q));  // open: clr
  Register #(.width(16)) R3 (.D(WDz), .en(decoder_1_out3), .clk(Wz), .Q(R3_q));  // open: clr
  Register #(.width(16)) R4 (.D(WDz), .en(decoder_1_out4), .clk(Wz), .Q(R4_q));  // open: clr
  Register #(.width(16)) R5 (.D(WDz), .en(decoder_1_out5), .clk(Wz), .Q(R5_q));  // open: clr
  Register #(.width(16)) R6 (.D(WDz), .en(decoder_1_out6), .clk(Wz), .Q(R6_q));  // open: clr
  Register #(.width(16)) R7 (.D(WDz), .en(decoder_1_out7), .clk(Wz), .Q(R7_q));  // open: clr
  Register #(.width(16)) R8 (.D(WDz), .en(decoder_1_out8), .clk(Wz), .Q(R8_q));  // open: clr
  Register #(.width(16)) R9 (.D(WDz), .en(decoder_1_out9), .clk(Wz), .Q(R9_q));  // open: clr
  Register #(.width(16)) R10 (.D(WDz), .en(decoder_1_out10), .clk(Wz), .Q(R10_q));  // open: clr
  Register #(.width(16)) R11 (.D(WDz), .en(decoder_1_out11), .clk(Wz), .Q(R11_q));  // open: clr
  Register #(.width(16)) R12 (.D(WDz), .en(decoder_1_out12), .clk(Wz), .Q(R12_q));  // open: clr
  Register #(.width(16)) R13 (.D(WDz), .en(decoder_1_out13), .clk(Wz), .Q(R13_q));  // open: clr
  Register #(.width(16)) R14 (.D(WDz), .en(decoder_1_out14), .clk(Wz), .Q(R14_q));  // open: clr
  Register #(.width(16)) R15 (.D(WDz), .en(decoder_1_out15), .clk(Wz), .Q(R15_q));  // open: clr
  Multiplexer #(.select(4), .width(16)) multiplexer_1 (
    .in0({16{1'b0}}), .in1(R1_q), .in2(R2_q), .in3(R3_q), .in4(R4_q), .in5(R5_q), .in6(R6_q), .in7(R7_q),
    .in8(R8_q), .in9(R9_q), .in10(R10_q), .in11(R11_q), .in12(R12_q), .in13(R13_q), .in14(R14_q),
    .in15(R15_q), .out(RDx), .sel(RAx));
  Multiplexer #(.select(4), .width(16)) multiplexer_2 (
    .in0({16{1'b0}}), .in1(R1_q), .in2(R2_q), .in3(R3_q), .in4(R4_q), .in5(R5_q), .in6(R6_q), .in7(R7_q),
    .in8(R8_q), .in9(R9_q), .in10(R10_q), .in11(R11_q), .in12(R12_q), .in13(R13_q), .in14(R14_q),
    .in15(R15_q), .out(RDy), .sel(RAy));
endmodule

module R16CPU (
);

  ROM #(.addrWidth(16), .dataWidth(16)) rom_1 ();  // open: addr, data
  R16File r16file_1 ();  // open: WDz, RAx, RAy, WAz, Wz, RDx, RDy
  RAM #(.addrWidth(16), .dataWidth(16), .databus("bidir")) ram_1 ();  // open: addr, we, oe, clk, data
endmodule

module Compts (
  input  [15:0] in_1,
  input  [3:0] in_2,
  input  [3:0] in_3,
  input  [3:0] in_4,
  input  in_5,
  output [15:0] out_6,
  output [15:0] out_7
);

  R16File r16file_1 (.WDz(in_1), .RAx(in_2), .RAy(in_3), .WAz(in_4), .Wz(in_5), .RDx(out_6), .RDy(out_7));
endmodule
