// Logisim project 07.gates.circ as structural Verilog: 1 circuit, main circuit main
module main (
);

  wire and_1_out, nor_1_out, not_1_out, or_1_out, undriven, undriven_2, undriven_3, undriven_4, undriven_5,
       undriven_6, undriven_7;

  not not_1 (not_1_out, undriven);
  and and_1 (and_1_out, undriven_2, undriven_3);
  or or_1 (or_1_out, undriven_4, undriven_5);
  nor nor_1 (nor_1_out, undriven_6, undriven_7);
endmodule
